# Fritzing sketch tiny13dev-breadboard (saved by Fritzing 0.7.12b)
breadboards: 1

parts:
  U1 = attiny85 [package=dip]
  U2 = Voltage Regulator - 5V [package="TO220 [THT]"]
  C2 = Electrolytic Capacitor [capacitance=10µF voltage=20V package="100 mil [THT, electrolytic]"]
  D1 = Rectifier Diode [part_number=1N4001 package="300 mil [THT]"]
  S1 = Toggle Switch [package=THT]
  VCC1 = Battery block 9V
  C1 = Electrolytic Capacitor [capacitance=0.1mF voltage=20V package="100 mil [THT, electrolytic]"]
  LED1 = LED - 5mm [color="Red (633nm)" package="5 mm [THT]"]
  J1 = shrouded pin header, 6 pins [form="♂ (shrouded male)"]
  R2 = Resistor [tolerance=±5% resistance=220 package=THT]
  R3 = Resistor [tolerance=±5% resistance=220 package=THT]
  S2 = Pushbutton [package="[THT]"]
  S3 = Pushbutton [package="[THT]"]
  R6 = Rotary Potentiometer (Small) [maximum_resistance=100kΩ]
  Q1 = NPN-Transistor [package="TO92 [THT]"]
  R7 = Resistor [tolerance=±5% resistance=22k package=THT]
  R8 = Resistor [tolerance=±5% resistance=22k package=THT]
  LED2 = LED - 5mm [color="Yellow (595nm)" package="5 mm [THT]"]
  Q2 = NPN-Transistor [package="TO92 [THT]"]
  LED3 = LED - 5mm [color="Green (555nm)" package="5 mm [THT]"]
  R9 = Resistor [tolerance=±5% resistance=220 package=THT]

nets:
  N1: U1.Pin_2, J1.pin2, S2.Pin_3, S2.Pin_4
  N2: U1.Pin_3, R6.wiper
  N3: U1.Pin_4, U2.GND, C2.-, C1.-, LED1.cathode, J1.pin4, S2.Pin_1, S2.Pin_2, S3.Pin_1, S3.Pin_2, R6.leg2, Q1.E, Q2.E
  N4: U1.Pin_5, J1.pin5, R7.Pin_0
  N5: U1.Pin_6, J1.pin1, R8.Pin_0
  N6: U2.input_voltage, S1.L2, C1.+
  N7: U2.output_voltage, C2.+, J1.pin6, R6.leg1, R9.Pin_1
  N8: D1.cathode, S1.COM
  N9: D1.anode, VCC1.-, VCC1.+, LED2.anode, LED3.anode
  N10: LED1.anode, R9.Pin_0
  N11: R2.Pin_0, LED2.cathode
  N12: R2.Pin_1, Q1.C
  N13: R3.Pin_0, LED3.cathode
  N14: R3.Pin_1, Q2.C
  N15: S3.Pin_3, S3.Pin_4
  N16: Q1.B, R8.Pin_1
  N17: R7.Pin_1, Q2.B

notes:
  ICSP6 connector for ISP programming
  5V rail
